// Logisim project cpu.circ as structural Verilog: 6 circuits, main circuit CPU
module CPU (
  input  MC_E,
  input  MOV_E,
  input  R_EN,
  input  IS32,
  input  [15:0] INSTR
);

  wire ALU_RW, button_1_out, CIN, CLK, not_1_out, not_2_out, R_WE;
  wire [2:0] counter_1_q;
  wire [3:0] BLOCKA, MC_ADDR, MCADDR, R_AD;
  wire [31:0] ADDR_BUS, DATA_BUS, R_DB;

  assign ADDR_BUS = IS32 ? R_DB : 32'bz;  // Controlled_Buffer controlled_buffer_1
  not not_1 (not_1_out, IS32);
  assign DATA_BUS = not_1_out ? R_DB : 32'bz;  // Controlled_Buffer controlled_buffer_2
  assign R_DB = DATA_BUS;  // Buffer buffer_1, 32 bits wide
  Clock clock_1 (.out(CLK));
  REGS regs_1 (.ADDR(R_AD), .DATA_IN(R_DB), .DATA_OUT(R_DB), .ENA(R_EN), .CLK(CLK), .IS32(IS32), .WE(R_WE));
  ALU alu_1 (.OPCODE(INSTR[15:12]), .RW(CIN), .CLK(ALU_RW), .ENA(CLK));  // open: DATA_IN, DATA_OUT
  Button button_1 (.out(button_1_out));
  assign MCADDR = MOV_E ? BLOCKA : 4'bz;  // Controlled_Buffer controlled_buffer_3
  not not_2 (not_2_out, MOV_E);
  assign MCADDR = not_2_out ? INSTR[15:12] : 4'bz;  // Controlled_Buffer controlled_buffer_4
  Counter #(.width(3), .max('h7)) counter_1 (
    .count(button_1_out), .Q(counter_1_q), .clk(button_1_out));  // open: load, D, carry, clr
  ROM rom_1 (.addr({MOV_E, MC_ADDR, counter_1_q}), .sel(MC_E));  // open: data

  // Other names for the same wires on the sheet: EN32 = IS32; BLOCKC[3:0] = INSTR[3:0]; BLOCKB[3:0] = INSTR[7:4];
  //   OPCODE[3:0] = INSTR[15:12]

  // Notes on the sheet:
  //   R_EN: pull=down
  //   MOV_E: pull=down
  //   MC_E: pull=down
  //   INSTR: pull=down
  //   IS32: pull=down
endmodule

module REG32 (
  input  [1:0] ADDR,
  input  [31:0] DATA_IN,
  input  ENA,
  input  RW,
  input  IS32,
  input  CLK,
  output [31:0] DATA_OUT
);

  wire and_1_out, and_2_out, and_3_out, and_4_out, and_5_out, and_6_out, and_7_out, and_8_out, and_9_out,
       and_10_out, controlled_buffer_9_out, controlled_buffer_12_out, controlled_buffer_19_out,
       controlled_buffer_24_out, decoder_1_out0, decoder_1_out1, decoder_1_out2, decoder_1_out3, not_1_out;
  wire [7:0] controlled_buffer_5_out, controlled_buffer_10_out, controlled_buffer_15_out,
       controlled_buffer_20_out, LH_q, LL_q, UH_q, UL_q;
  wire [31:0] controlled_buffer_1_out, controlled_buffer_3_out, pull_resistor_1_node;

  Decoder #(.select(2), .enable("false")) decoder_1 (
    .out0(decoder_1_out0), .out1(decoder_1_out1), .out2(decoder_1_out2), .out3(decoder_1_out3), .sel(ADDR));
  Pull_Resistor pull_resistor_1 (.node(pull_resistor_1_node));
  assign controlled_buffer_1_out = not_1_out ? pull_resistor_1_node : 32'bz;  // Controlled_Buffer controlled_buffer_1
  assign DATA_OUT = ENA ? controlled_buffer_1_out : 32'bz;  // Controlled_Buffer controlled_buffer_2
  not not_1 (not_1_out, RW);
  assign controlled_buffer_3_out = ENA ? DATA_IN : 32'bz;  // Controlled_Buffer controlled_buffer_3
  assign pull_resistor_1_node = RW ? controlled_buffer_3_out : 32'bz;  // Controlled_Buffer controlled_buffer_4
  and and_1 (and_1_out, decoder_1_out3, ~IS32, RW);  // AND_Gate
  assign controlled_buffer_5_out = and_1_out ? pull_resistor_1_node[7:0] : 8'bz;  // Controlled_Buffer controlled_buffer_5
  assign pull_resistor_1_node[7:0] = and_4_out ? UH_q : 8'bz;  // Controlled_Buffer controlled_buffer_6
  Register UH (.D(controlled_buffer_5_out), .Q(UH_q), .clk(controlled_buffer_9_out));  // open: en, clr
  assign controlled_buffer_5_out = and_2_out ? pull_resistor_1_node[31:24] : 8'bz;  // Controlled_Buffer controlled_buffer_7
  and and_2 (and_2_out, RW, IS32);
  and and_3 (and_3_out, IS32, ~RW);  // AND_Gate
  assign pull_resistor_1_node[31:24] = and_3_out ? UH_q : 8'bz;  // Controlled_Buffer controlled_buffer_8
  assign controlled_buffer_9_out = ENA ? CLK : 1'bz;  // Controlled_Buffer controlled_buffer_9
  and and_4 (and_4_out, decoder_1_out3, ~IS32, ~RW);  // AND_Gate
  and and_5 (and_5_out, decoder_1_out2, ~IS32, RW);  // AND_Gate
  assign controlled_buffer_10_out = and_5_out ? pull_resistor_1_node[7:0] : 8'bz;  // Controlled_Buffer controlled_buffer_10
  assign controlled_buffer_10_out = and_2_out ? pull_resistor_1_node[23:16] : 8'bz;  // Controlled_Buffer controlled_buffer_11
  assign controlled_buffer_12_out = ENA ? CLK : 1'bz;  // Controlled_Buffer controlled_buffer_12
  assign pull_resistor_1_node[7:0] = and_6_out ? UL_q : 8'bz;  // Controlled_Buffer controlled_buffer_13
  and and_6 (and_6_out, decoder_1_out2, ~IS32, ~RW);  // AND_Gate
  Register UL (.D(controlled_buffer_10_out), .Q(UL_q), .clk(controlled_buffer_12_out));  // open: en, clr
  assign pull_resistor_1_node[23:16] = and_3_out ? UL_q : 8'bz;  // Controlled_Buffer controlled_buffer_14
  and and_7 (and_7_out, decoder_1_out1, ~IS32, RW);  // AND_Gate
  assign controlled_buffer_15_out = and_7_out ? pull_resistor_1_node[7:0] : 8'bz;  // Controlled_Buffer controlled_buffer_15
  assign controlled_buffer_15_out = and_2_out ? pull_resistor_1_node[15:8] : 8'bz;  // Controlled_Buffer controlled_buffer_16
  assign pull_resistor_1_node[7:0] = and_8_out ? LH_q : 8'bz;  // Controlled_Buffer controlled_buffer_17
  and and_8 (and_8_out, decoder_1_out1, ~IS32, ~RW);  // AND_Gate
  Register LH (.D(controlled_buffer_15_out), .Q(LH_q), .clk(controlled_buffer_19_out));  // open: en, clr
  assign pull_resistor_1_node[15:8] = and_3_out ? LH_q : 8'bz;  // Controlled_Buffer controlled_buffer_18
  assign controlled_buffer_19_out = ENA ? CLK : 1'bz;  // Controlled_Buffer controlled_buffer_19
  and and_9 (and_9_out, decoder_1_out0, ~IS32, RW);  // AND_Gate
  assign controlled_buffer_20_out = and_9_out ? pull_resistor_1_node[7:0] : 8'bz;  // Controlled_Buffer controlled_buffer_20
  assign pull_resistor_1_node[7:0] = and_10_out ? LL_q : 8'bz;  // Controlled_Buffer controlled_buffer_21
  and and_10 (and_10_out, decoder_1_out0, ~IS32, ~RW);  // AND_Gate
  Register LL (.D(controlled_buffer_20_out), .Q(LL_q), .clk(controlled_buffer_24_out));  // open: en, clr
  assign controlled_buffer_20_out = and_2_out ? pull_resistor_1_node[7:0] : 8'bz;  // Controlled_Buffer controlled_buffer_22
  assign pull_resistor_1_node[7:0] = and_3_out ? LL_q : 8'bz;  // Controlled_Buffer controlled_buffer_23
  assign controlled_buffer_24_out = ENA ? CLK : 1'bz;  // Controlled_Buffer controlled_buffer_24

  // Notes on the sheet:
  //   ADDR: pull=down
  //   RW: pull=down
  //   CLK: pull=down
  //   DATA_OUT: pull=down
  //   ENA: pull=down
  //   DATA_IN: pull=down
  //   IS32: pull=down
endmodule

module REGS (
  input  [3:0] ADDR,
  input  [31:0] DATA_IN,
  input  ENA,
  input  CLK,
  input  IS32,
  input  WE,
  output [31:0] DATA_OUT
);

  wire A_ENA, B_ENA, C_ENA, D_ENA, not_1_out;
  wire [31:0] controlled_buffer_1_out, controlled_buffer_2_out, DATA;

  REG32 reg32_1 (.ADDR(ADDR[3:2]), .DATA_OUT(DATA), .DATA_IN(DATA), .ENA(A_ENA), .RW(WE), .IS32(IS32), .CLK(CLK));
  assign controlled_buffer_1_out = ENA ? DATA_IN : 32'bz;  // Controlled_Buffer controlled_buffer_1
  assign controlled_buffer_2_out = not_1_out ? DATA : 32'bz;  // Controlled_Buffer controlled_buffer_2
  assign DATA_OUT = ENA ? controlled_buffer_2_out : 32'bz;  // Controlled_Buffer controlled_buffer_3
  not not_1 (not_1_out, WE);
  Decoder #(.select(2), .disabled(0)) decoder_1 (
    .out0(A_ENA), .out1(B_ENA), .out2(C_ENA), .out3(D_ENA), .sel(ADDR[1:0]), .en(ENA));
  REG32 reg32_2 (.ADDR(ADDR[3:2]), .DATA_OUT(DATA), .DATA_IN(DATA), .ENA(B_ENA), .RW(WE), .IS32(IS32), .CLK(CLK));
  assign DATA = WE ? controlled_buffer_1_out : 32'bz;  // Controlled_Buffer controlled_buffer_4
  REG32 reg32_3 (.ADDR(ADDR[3:2]), .DATA_OUT(DATA), .DATA_IN(DATA), .ENA(C_ENA), .RW(WE), .IS32(IS32), .CLK(CLK));
  REG32 reg32_4 (.ADDR(ADDR[3:2]), .DATA_OUT(DATA), .DATA_IN(DATA), .ENA(D_ENA), .RW(WE), .IS32(IS32), .CLK(CLK));

  // Other names for the same wires on the sheet: L_ADDR[1:0] = ADDR[1:0]; H_ADDR[1:0] = ADDR[3:2]

  // Notes on the sheet:
  //   ADDR: pull=down
  //   DATA_IN: pull=down
  //   IS32: pull=down
  //   CLK: pull=down
  //   ENA: pull=down
  //   DATA_OUT: pull=down
  //   WE: pull=down
endmodule

module ALU (
  input  [3:0] OPCODE,
  input  RW,
  input  CLK,
  input  ENA,
  input  [15:0] DATA_IN,
  output [7:0] DATA_OUT
);

  wire ADC, ADD, adder_1_cout, CARRY, CIN, controlled_buffer_1_out, COUT, LSC, LSH, lsh_1_cout, NAND, OE,
       or_1_out, or_2_out, or_3_out, or_4_out, or_5_out, or_6_out, RSC, RSH, rsh_1_cout, SBC, SUB,
       subtractor_1_bout, undriven, XOR;
  wire [7:0] adder_1_out, lsh_1_out, nand_1_out, rsh_1_out, subtractor_1_out, xor_1_out;
  wire [15:0] register_2_q;

  assign controlled_buffer_1_out = ENA ? RW : 1'bz;  // Controlled_Buffer controlled_buffer_1
  Register #(.width(1), .trigger("falling")) register_1 (
    .D(or_1_out), .en(undriven), .Q(CARRY), .clk(CLK));  // open: clr
  or or_1 (or_1_out, ADD, SUB, LSH, RSH, ADC, SBC, LSC, RSC);
  Pull_Resistor pull_resistor_1 (.node(CIN));
  assign CIN = or_2_out ? CARRY : 1'bz;  // Controlled_Buffer controlled_buffer_2
  or or_2 (or_2_out, ADC, SBC, LSC, RSC);
  Register #(.width(16)) register_2 (
    .D(DATA_IN), .en(controlled_buffer_1_out), .Q(register_2_q), .clk(CLK));  // open: clr
  or or_3 (or_3_out, ADD, ADC);
  assign DATA_OUT = or_3_out ? adder_1_out : 8'bz;  // Controlled_Buffer controlled_buffer_3
  Adder adder_1 (.a(register_2_q[7:0]), .b(register_2_q[15:8]), .out(adder_1_out), .cin(CIN), .cout(adder_1_cout));
  assign COUT = or_3_out ? adder_1_cout : 1'bz;  // Controlled_Buffer controlled_buffer_4
  or or_4 (or_4_out, SUB, SBC);
  assign DATA_OUT = or_4_out ? subtractor_1_out : 8'bz;  // Controlled_Buffer controlled_buffer_5
  Subtractor subtractor_1 (
    .a(register_2_q[7:0]), .b(register_2_q[15:8]), .out(subtractor_1_out), .bin(CIN), .bout(subtractor_1_bout));
  assign COUT = or_4_out ? subtractor_1_bout : 1'bz;  // Controlled_Buffer controlled_buffer_6
  or or_5 (or_5_out, LSH, LSC);
  LSH lsh_1 (.OUT(lsh_1_out), .IN(register_2_q[7:0]), .CIN(CIN), .COUT(lsh_1_cout));
  assign DATA_OUT = or_5_out ? lsh_1_out : 8'bz;  // Controlled_Buffer controlled_buffer_7
  assign COUT = or_5_out ? lsh_1_cout : 1'bz;  // Controlled_Buffer controlled_buffer_8
  or or_6 (or_6_out, RSH, RSC);
  RSH rsh_1 (.OUT(rsh_1_out), .COUT(rsh_1_cout), .CIN(CIN), .IN(register_2_q[7:0]));
  assign DATA_OUT = or_6_out ? rsh_1_out : 8'bz;  // Controlled_Buffer controlled_buffer_9
  assign COUT = or_6_out ? rsh_1_cout : 1'bz;  // Controlled_Buffer controlled_buffer_10
  assign xor_1_out = register_2_q[7:0] ^ register_2_q[15:8];  // XOR_Gate xor_1, 8 bits wide
  assign DATA_OUT = XOR ? xor_1_out : 8'bz;  // Controlled_Buffer controlled_buffer_11
  assign DATA_OUT = NAND ? nand_1_out : 8'bz;  // Controlled_Buffer controlled_buffer_12
  assign nand_1_out = ~(register_2_q[7:0] & register_2_q[15:8]);  // NAND_Gate nand_1, 8 bits wide
  and and_1 (OE, CLK, ~RW, ENA);  // AND_Gate
  Decoder #(.select(4), .disabled(0)) decoder_1 (
    .out0(ADD), .out1(ADC), .out2(SUB), .out3(SBC), .out4(LSH), .out5(LSC), .out6(RSH), .out7(RSC),
    .out8(XOR), .out9(NAND), .sel(OPCODE), .en(OE));  // open: out10, out11, out12, out13, out14, out15

  // Other names for the same wires on the sheet: CE = ENA

  // Notes on the sheet:
  //   CLK: pull=down
  //   ENA: pull=down
  //   DATA_IN: pull=down
  //   RW: pull=down
  //   DATA_OUT: pull=down
  //   OPCODE: pull=down
endmodule

module LSH (
  input  [7:0] IN,
  input  CIN,
  output COUT,
  output [7:0] OUT
);

  Pull_Resistor pull_resistor_1 (.node(IN[7]));

  assign COUT = IN[7];
  assign OUT = {IN[6:0], CIN};

  // Notes on the sheet:
  //   CIN: pull=down
  //   COUT: pull=down
  //   OUT: pull=down
  //   IN: pull=down
endmodule

module RSH (
  input  CIN,
  input  [7:0] IN,
  output [7:0] OUT,
  output COUT
);

  Pull_Resistor pull_resistor_1 (.node(IN[0]));

  assign COUT = IN[0];
  assign OUT = {CIN, IN[7:1]};

  // Notes on the sheet:
  //   OUT: pull=down
  //   CIN: pull=down
  //   IN: pull=down
  //   COUT: pull=down
endmodule
